# Fritzing sketch velociruabtor_v2_tht (saved by Fritzing 0.9.3b)
perfboards: 1

parts:
  J5 = female pin header, 3 pins [form="♀ (female)"]
  J6 = female pin header, 8 pins [form="♀ (female)"]
  J7 = female pin header, 8 pins [form="♀ (female)"]
  J9 = female pin header, 14 pins [form="♀ (female)"]
  J10 = female pin header, 14 pins [form="♀ (female)"]
  J12 = female pin header, 3 pins [form="♀ (female)"]
  J20 = female pin header, 6 pins [form="♀ (female)"]
  J21 = female pin header, 6 pins [form="♀ (female)"]
  J8 = female pin header, 8 pins [form="♀ (female)"]
  J25 = female pin header, 2 pins [form="♀ (female)"]
  J14 = female pin header, 6 pins [form="♀ (female)"]
  J13 = female pin header, 6 pins [form="♀ (female)"]
  J26 = female pin header, 1 pin [form="♀ (female)"]  # not connected

nets:
  N1: J5.pin1, J6.pin7, J12.pin1
  N2: J5.pin2, J21.pin6
  N3: J5.pin3, J6.pin2, J9.pin1, J14.pin2
  N4: J6.pin1, J10.pin1, J20.pin1, J25.pin2, J13.pin2
  N5: J6.pin3, J21.pin1
  N6: J6.pin4, J21.pin2
  N7: J6.pin5, J20.pin5
  N8: J6.pin6, J20.pin6
  N9: J7.pin1, J10.pin5
  N10: J7.pin2, J10.pin6
  N11: J7.pin3, J10.pin7
  N12: J7.pin4, J10.pin8
  N13: J7.pin5, J10.pin9
  N14: J7.pin6, J10.pin10
  N15: J7.pin7, J10.pin11
  N16: J9.pin4, J8.pin1
  N17: J9.pin5, J8.pin2
  N18: J9.pin6, J8.pin3
  N19: J9.pin7, J8.pin4
  N20: J9.pin8, J8.pin5
  N21: J9.pin9, J8.pin6
  N22: J9.pin10, J8.pin7
  N23: J9.pin11, J8.pin8
  N24: J9.pin12, J13.pin3
  N25: J9.pin13, J13.pin4
  N26: J9.pin14, J13.pin6
  N27: J10.pin2, J14.pin4
  N28: J10.pin3, J14.pin5
  N29: J10.pin4, J21.pin4
  N30: J10.pin12, J21.pin5
  N31: J10.pin13, J20.pin3
  N32: J10.pin14, J20.pin2
  N33: J20.pin4, J25.pin1
